# Fritzing sketch Esquematico_v2 (saved by Fritzing 0.9.3b)
breadboards: 1

parts:
  J1 = STM32 Nucleo boards
  Componente1 = LilyPad Coin Cell Battery Holder
  RHT1 = Humidity and Temperature Sensor RHT03
  U2 = RELAY-2 [package=relay-g5v]  # not connected
  U3 = RELAY-2 [package=relay-g5v]  # not connected
  U4 = RELAY-2 [package=relay-g5v]  # not connected
  U5 = RELAY-2 [package=relay-g5v]  # not connected
  U6 = RELAY-2 [package=relay-g5v]  # not connected
  Capacitive_Soil_Moisture_Sensor1 = Capacitive Soil Moisture Sensor V2.0
  Capacitive_Soil_Moisture_Sensor2 = Capacitive Soil Moisture Sensor V2.0
  Capacitive_Soil_Moisture_Sensor3 = Capacitive Soil Moisture Sensor V2.0
  Capacitive_Soil_Moisture_Sensor4 = Capacitive Soil Moisture Sensor V2.0
  Capacitive_Soil_Moisture_Sensor5 = Capacitive Soil Moisture Sensor V2.0
  8_Channel_Relay1 = 8 Channel Power Relay
  U7 = RELAY-2 [package=relay-g5v]  # not connected
  U8 = RELAY-2 [package=relay-g5v]  # not connected
  U9 = RELAY-2 [package=relay-g5v]  # not connected
  C1 = Capacitor Polarized [package=cpol-radial-10uf-25v]
  JACK1 = 2.1mm Barrel Jack with Terminal Block
  S5 = Momentary Switch [package=ksa_sealed_tac_switch]
  S6 = Pushbutton [package="[SMD]"]
  OLED1 = OLED 128x64 I2C Monochrome Display
  VALVE2 = Plastic Solenoid Valve
  VALVE1 = Plastic Solenoid Valve
  J3 = Screw terminal - 2 pins [package=THT]
  R1 = Resistor [tolerance=±5% resistance=220 package=THT]
  C2 = Ceramic Capacitor [capacitance=100nF package="100 mil [THT, multilayer]"]
  R2 = Resistor [tolerance=±5% resistance=220 package=THT]

nets:
  N1: J1.A1, Capacitive_Soil_Moisture_Sensor5.AOUT
  N2: J1.A2, Capacitive_Soil_Moisture_Sensor4.AOUT
  N3: J1.A3, Capacitive_Soil_Moisture_Sensor3.AOUT
  N4: J1.A4/SDA, Capacitive_Soil_Moisture_Sensor2.AOUT
  N5: J1.A5/SCL, Capacitive_Soil_Moisture_Sensor1.AOUT
  VCC: J1.E5V, Capacitive_Soil_Moisture_Sensor1.VCC, Capacitive_Soil_Moisture_Sensor2.VCC, Capacitive_Soil_Moisture_Sensor3.VCC, Capacitive_Soil_Moisture_Sensor4.VCC, Capacitive_Soil_Moisture_Sensor5.VCC, 8_Channel_Relay1.VCC, C1.+, JACK1.POS, OLED1.VDD, R1.Pin_1
  GND: J1.GND#333, Capacitive_Soil_Moisture_Sensor1.GND, Capacitive_Soil_Moisture_Sensor2.GND, Capacitive_Soil_Moisture_Sensor3.GND, Capacitive_Soil_Moisture_Sensor4.GND, Capacitive_Soil_Moisture_Sensor5.GND, 8_Channel_Relay1.GND, C1.-, JACK1.NEG, S5.4, OLED1.GND, C2.1
  3V3: J1.3v3, RHT1.Vcc
  N6: J1.GND#339, RHT1.GND_2
  N7: J1.PB8, OLED1.SCK
  N8: J1.PB9, OLED1.SDA
  N9: J1.PA7, 8_Channel_Relay1.IN1
  N10: J1.PB6, 8_Channel_Relay1.IN2
  N11: J1.PC7, 8_Channel_Relay1.IN3
  N12: J1.PA9, 8_Channel_Relay1.IN4
  N13: J1.PA8, 8_Channel_Relay1.IN5
  N14: J1.PB10, 8_Channel_Relay1.IN6
  N15: J1.PB4, 8_Channel_Relay1.IN7
  N16: J1.PB5, 8_Channel_Relay1.IN8
  N17: J1.GND#3310, Componente1.-
  N18: J1.PC12, RHT1.Data-signal
  N19: J1.VLCD, Componente1.+
  N20: 8_Channel_Relay1.COM, J3.pin1
  N21: 8_Channel_Relay1.NO#23, VALVE1.no_name_yet#2
  N22: 8_Channel_Relay1.NO#26, VALVE2.no_name_yet#2
  N23: S5.1, R2.Pin_0
  N24: S5.2, R1.Pin_0
  N25: S6.Pin_1, S6.Pin_2
  N26: S6.Pin_3, S6.Pin_4
  N27: VALVE2.no_name_yet#1, VALVE1.no_name_yet#1, J3.pin2

notes:
  JP5 (5V_SEL): E5V

custom parts:
  8 Channel Power Relay: An 8 channel power relay. The module operates at 5V.
